# Fritzing sketch CPBO Schéma électrique (saved by Fritzing 0.9.3b)

parts:
  U1 = PCF8574 [package="DIP16 [THT]"]
  U2 = PCF8574 [package="DIP16 [THT]"]
  U3 = PCF8574 [package="DIP16 [THT]"]
  U4 = PCF8574 [package="DIP16 [THT]"]
  U5 = PCF8574 [package="DIP16 [THT]"]
  Composant1 = Arduino Pro Micro (Clone)
  U6 = POT [package=pot_alpha_rv16af-20]
  RE1 = KY-040 Rotary encoder [package=THT]
  LED3 = LED - 5mm [color="Red (633nm)" package="5 mm [THT]"]
  S3 = Toggle Switch spdt [package=THT]
  S4 = Toggle Switch spst [package=THT]
  LED8 = LED - 5mm [color="Red (633nm)" package="5 mm [THT]"]
  S5 = Toggle Switch spst [package=THT]
  LED9 = LED - 5mm [color="Red (633nm)" package="5 mm [THT]"]
  S6 = Toggle Switch spst [package=THT]
  S7 = Toggle Switch spdt [package=THT]
  S8 = Toggle Switch spdt [package=THT]
  S9 = Toggle Switch spdt [package=THT]
  LED11 = LED - 5mm [color="Yellow (595nm)" package="5 mm [THT]"]
  S15 = Toggle Switch spst [package=THT]
  LED12 = LED - 5mm [color="Yellow (595nm)" package="5 mm [THT]"]
  S16 = Toggle Switch spst [package=THT]
  LED13 = LED - 5mm [color="Green (565nm)" package="5 mm [THT]"]
  S17 = Toggle Switch spst [package=THT]
  LED14 = LED - 5mm [color="Blue (470nm)" package="5 mm [THT]"]
  S18 = Toggle Switch spst [package=THT]
  LED15 = LED - 5mm [color="Blue (470nm)" package="5 mm [THT]"]
  S19 = Toggle Switch spst [package=THT]
  LED16 = LED - 5mm [color="Blue (470nm)" package="5 mm [THT]"]
  S20 = Toggle Switch spst [package=THT]
  U7 = POT [package=pot_alpha_rv16af-20]
  LED17 = LED - 5mm [color="Blue (470nm)" package="5 mm [THT]"]
  S21 = Toggle Switch spst [package=THT]
  LED18 = LED - 5mm [color="Blue (470nm)" package="5 mm [THT]"]
  S22 = Toggle Switch spst [package=THT]
  LED19 = LED - 5mm [color="Blue (470nm)" package="5 mm [THT]"]
  S23 = Toggle Switch spst [package=THT]
  LED20 = LED - 5mm [color="Blue (470nm)" package="5 mm [THT]"]
  S24 = Toggle Switch spst [package=THT]
  LED21 = LED - 5mm [color="Blue (470nm)" package="5 mm [THT]"]
  S25 = Toggle Switch spst [package=THT]
  LED22 = LED - 5mm [color="Blue (470nm)" package="5 mm [THT]"]
  S26 = Toggle Switch spst [package=THT]
  LED23 = LED - 5mm [color="Blue (470nm)" package="5 mm [THT]"]
  S27 = Toggle Switch spst [package=THT]
  LED24 = LED - 5mm [color="Blue (470nm)" package="5 mm [THT]"]
  S28 = Toggle Switch spst [package=THT]
  LED25 = LED - 5mm [color="Blue (470nm)" package="5 mm [THT]"]
  S29 = Toggle Switch spst [package=THT]
  LED26 = LED - 5mm [color="Blue (470nm)" package="5 mm [THT]"]
  S30 = Toggle Switch spst [package=THT]
  LED27 = LED - 5mm [color="Blue (470nm)" package="5 mm [THT]"]
  S31 = Toggle Switch spst [package=THT]
  LED28 = LED - 5mm [color="Blue (470nm)" package="5 mm [THT]"]
  S32 = Toggle Switch spst [package=THT]
  LED29 = LED - 5mm [color="Blue (470nm)" package="5 mm [THT]"]
  S33 = Toggle Switch spst [package=THT]
  LED30 = LED - 5mm [color="Blue (470nm)" package="5 mm [THT]"]
  S34 = Toggle Switch spst [package=THT]
  LED31 = LED - 5mm [color="Blue (470nm)" package="5 mm [THT]"]
  S35 = Toggle Switch spst [package=THT]
  LED32 = LED - 5mm [color="Blue (470nm)" package="5 mm [THT]"]
  S36 = Toggle Switch spst [package=THT]
  LED33 = LED - 5mm [color="Blue (470nm)" package="5 mm [THT]"]
  S37 = Toggle Switch spst [package=THT]
  LED34 = LED - 5mm [color="Green (565nm)" package="5 mm [THT]"]
  S38 = Toggle Switch spst [package=THT]
  LED35 = LED - 5mm [color="Green (565nm)" package="5 mm [THT]"]
  S39 = Toggle Switch spst [package=THT]
  LED36 = LED - 5mm [color="Green (565nm)" package="5 mm [THT]"]
  S40 = Toggle Switch spst [package=THT]
  LED37 = LED - 5mm [color="Yellow (595nm)" package="5 mm [THT]"]
  S41 = Toggle Switch spst [package=THT]
  LED38 = LED - 5mm [color="Yellow (595nm)" package="5 mm [THT]"]
  S42 = Toggle Switch spst [package=THT]
  LED39 = LED - 5mm [color="Yellow (595nm)" package="5 mm [THT]"]
  S43 = Toggle Switch spst [package=THT]
  LED40 = LED - 5mm [color="Yellow (595nm)" package="5 mm [THT]"]
  S44 = Toggle Switch spst [package=THT]
  LED41 = LED - 5mm [color="Red (633nm)" package="5 mm [THT]"]
  S45 = Toggle Switch spst [package=THT]
  S46 = Toggle Switch spst [package=THT]
  LED43 = LED - 5mm [color="White (4500K)" package="5 mm [THT]"]
  S47 = Toggle Switch spst [package=THT]
  LED44 = LED - 5mm [color="White (4500K)" package="5 mm [THT]"]
  S48 = Toggle Switch spst [package=THT]
  LED45 = LED - 5mm [color="Red (633nm)" package="5 mm [THT]"]

nets:
  VCC: U1.A2, U1.VCC, U2.A0, U2.A1, U2.VCC, U3.A1, U3.VCC, U4.A0, U4.A1, U4.VCC, U5.VCC, Composant1.VCC, U6.E, RE1.Vcc, U7.E
  N1: U1.P0, S18.L1
  N2: U1.P1, S19.L1
  N3: U1.P2, S20.L1
  N4: U1.P3, S15.L1
  GND: U1.GND, U2.GND, U3.GND, U4.GND, U5.GND, Composant1.RXI, Composant1.GND, Composant1.RST, U6.A, RE1.GND, RE1.CLK, S3.COM, S7.COM, S8.COM, S9.COM, LED11.cathode, S15.COM, LED12.cathode, S16.COM, LED13.cathode, S17.COM, LED14.cathode, S18.COM, LED15.cathode, S19.COM, LED16.cathode, S20.COM, U7.A, LED21.cathode, S25.COM, LED22.cathode, S26.COM, LED23.cathode, S27.COM, LED24.cathode, S28.COM, LED25.cathode, S29.COM, LED26.cathode, S30.COM, LED27.cathode, S31.COM, LED28.cathode, S32.COM, LED31.cathode, S35.COM, LED32.cathode, S36.COM, LED33.cathode, S37.COM, LED34.cathode, S38.COM, LED35.cathode, S39.COM, LED37.cathode, S41.COM, LED38.cathode, S42.COM, LED39.cathode, S43.COM, LED40.cathode, S44.COM, LED41.cathode, S45.COM, S46.COM, LED43.cathode, S47.COM, LED44.cathode, S48.COM, LED45.cathode
  N5: U1.P4, S16.L1
  N6: U1.P5, S17.L1
  N7: U1.SCL, U2.SCL, U3.SCL, U4.SCL, U5.SCL, Composant1.D3
  N8: U1.SDA, U2.SDA, U3.SDA, U4.SDA, U5.SDA, Composant1.D2
  N9: U2.P0, S39.L1
  N10: U2.P1, S28.L1
  N11: U2.P2, S27.L1
  N12: U2.P3, S48.L1
  N13: U2.P4, S26.L1
  N14: U2.P5, S25.L1
  N15: U2.P6, S38.L1
  N16: U3.A2, U3.P0, S21.L1
  N17: U3.P1, S22.L1
  N18: U3.P2, S23.L1
  N19: U3.P3, S24.L1
  N20: U3.P4, S47.L1
  N21: U3.P5, S31.L1
  N22: U3.P6, S29.L1
  N23: U3.P7, U3.INT, S30.L1
  N24: U4.A2, U4.P0, S34.L1
  N25: U4.P1, S41.L1
  N26: U4.P2, S42.L1
  N27: U4.P3, S43.L1
  N28: U4.P4, S44.L1
  N29: U4.P5, S32.L1
  N30: U4.P6, S45.L1
  N31: U4.P7, U4.INT, S46.L1
  N32: U5.A2, U5.P0, S3.L2
  N33: U5.P1, S3.L1
  N34: U5.P2, S9.L2
  N35: U5.P3, S9.L1
  N36: U5.P4, S8.L2
  N37: U5.P5, S8.L1
  N38: U5.P6, S7.L2
  N39: U5.P7, U5.INT, S7.L1
  N40: Composant1.TXO, RE1.DT
  N41: Composant1.D4, LED9.anode
  N42: Composant1.D5, S6.L1
  N43: Composant1.D6, LED8.anode
  N44: Composant1.D7, S5.L1
  N45: Composant1.D8, LED3.anode
  N46: Composant1.D9, S4.L1
  N47: Composant1.D10, LED11.anode, LED12.anode, LED13.anode, LED14.anode, LED15.anode, LED16.anode, LED17.anode, LED18.anode, LED19.anode, LED20.anode, LED21.anode, LED22.anode, LED23.anode, LED24.anode, LED25.anode, LED26.anode, LED27.anode, LED28.anode, LED29.anode, LED30.anode, LED31.anode, LED32.anode, LED33.anode, LED34.anode, LED35.anode, LED36.anode, LED37.anode, LED38.anode, LED39.anode, LED40.anode, LED41.anode, LED43.anode, LED44.anode, LED45.anode
  N48: Composant1.D16, S33.L1
  N49: Composant1.D14, S40.L1
  N50: Composant1.D15, S37.L1
  N51: Composant1.A0, S36.L1
  N52: Composant1.A1, S35.L1
  N53: Composant1.A2, U6.S
  N54: Composant1.A3, U7.S
  N55: LED3.cathode, S4.COM, LED8.cathode, S5.COM, LED9.cathode, S6.COM, LED17.cathode, S21.COM, LED18.cathode, S22.COM, LED19.cathode, S23.COM, LED20.cathode, S24.COM, LED29.cathode, S33.COM, LED30.cathode, S34.COM, LED36.cathode, S40.COM

notes:
  JETTISON CARGO
  EJECT
  SELF DESTRUCT
  SCAN
  MINING
  LASER MODE
  1
  2
  BLEU
  3
  LASER POWER
  MINING CONSUMABLE
  LANDING
  QT TRAVEL
  V TOL
  QT DRIVE
  FRONT
  RIGHT
  LEFT
  BACK
  WEAPONS
  SHIELDS
  THRUST
  MATCH T.VEL
  MOTOR
  POWER
  OPEN DOORS
  LOCK DOORS
  LIGHTS
  TOP
  BOTTOM
  SYSTEM READY
  GIMBALS
  DECOUPLED
  E.S.P.
  G-FORCE
  DECOY
  NOISE
  RESET
  TARGETING
  ATT
  HOST
  FRIENDS
  ALL
  THROTTLE
  POWER MANAGEMENT
  SIELDS MANAGEMENT
  LED POWER

custom parts:
  KY-040 Rotary encoder: KY-040 Rotary Encoder with switch on breakout borad from AZ Delivery
  Toggle Switch spdt: Toggle Switch single pole double throw
  Toggle Switch spst: Toggle Switch single pole single throw
